# Fritzing sketch raspi-audio-button (saved by Fritzing 0.9.2b)
circuit board: 8.46667cm x 5.64444cm
breadboards: 1

parts:
  S1 = Pushbutton [package="[THT]"]
  S2 = Pushbutton [package="[THT]"]
  S3 = Pushbutton [package="[THT]"]
  R1 = Resistor [tolerance=±5% resistance=10k package=THT]
  R2 = Resistor [tolerance=±5% resistance=10k package=THT]
  R3 = Resistor [tolerance=±5% resistance=10k package=THT]
  RaspberryPi1 = Raspberry Pi Model B

nets:
  N1: S1.Pin_1, S1.Pin_2, S2.Pin_1, S2.Pin_2, S3.Pin_1, S3.Pin_2, RaspberryPi1.GND
  N2: S1.Pin_3, S1.Pin_4, R1.Pin_0, RaspberryPi1.#25
  N3: S2.Pin_3, S2.Pin_4, R2.Pin_0, RaspberryPi1.#24
  N4: S3.Pin_3, S3.Pin_4, R3.Pin_0, RaspberryPi1.#23
  N5: R1.Pin_1, R2.Pin_1, R3.Pin_1, RaspberryPi1.3V3

custom parts:
  Raspberry Pi Model B: Raspberry Pi (Model B)

// code stored in the sketch: raspi-audio-button.ino

